# Fritzing sketch monitor1 (saved by Fritzing 0.9.3b)
breadboards: 1

parts:
  Arduino_Nano = Arduino Nano (Rev3.0)
  U1 = Sharp PC817 [package=THT]
  J2-ws = Generic connector 1 Pin [form=male package=THT]
  J4-sw = Generic connector 1 Pin [form=male package=THT]
  R1 = Resistor [tolerance=±5% resistance=3.3k package=THT]
  R2 = Resistor [tolerance=±5% resistance=3.3k package=THT]
  J3 = Generic connector 1 Pin [form=male package=THT]  # not connected
  J1 = Generic connector 1 Pin [form=male package=THT]  # not connected
  JT1 = Generic connector 1 Pin [form=male package=THT]  # not connected
  JT2 = Generic connector 1 Pin [form=male package=THT]
  JT3 = Generic connector 1 Pin [form=male package=THT]  # not connected
  JT4 = Generic connector 1 Pin [form=male package=THT]
  U2 = Generic-4PinEdit [package=THT]
  +12V = Generic connector 1 Pin [form=male package=THT]
  GND = Generic connector 1 Pin [form=male package=THT]
  U3 = mystery part, 5 pins [chip_label=Relais]
  D+ = Generic connector 1 Pin [form=male package=THT]
  D1 = Rectifier Diode [part_number=1N4001 package="300 mil [THT]"]
  D2 = Rectifier Diode [part_number=1N4001 package="300 mil [THT]"]
  D+_Kühlschrank = Generic connector 1 Pin [form=male package=THT]
  original_D+ = Generic connector 1 Pin [form=male package=THT]
  original_D+_2 = Generic connector 1 Pin [form=male package=THT]

nets:
  GND: Arduino_Nano.GND, R2.Pin_1, JT4.pin1, U2.GND_OUT, U3.pin3
  N1: Arduino_Nano.D2, U1.Pin_3, R2.Pin_0
  N2: Arduino_Nano.D3, JT2.pin1
  N3: Arduino_Nano.D4, U3.pin2
  N4: Arduino_Nano.VIN, U2.+5
  N5: Arduino_Nano.5V, U1.Pin_4, U3.pin1
  N6: U1.Pin_1, R1.Pin_1
  N7: U1.Pin_2, J4-sw.pin1
  N8: J2-ws.pin1, R1.Pin_0
  N9: U2.+12V, +12V.pin1, U3.pin4
  N10: U2.GND_IN, GND.pin1
  N11: U3.pin5, D+.pin1
  N12: D1.cathode, D2.cathode, D+_Kühlschrank.pin1
  N13: D1.anode, original_D+.pin1
  N14: D2.anode, original_D+_2.pin1

notes:
  JST-PH 2.00mm pitch 4-pin connector female cable
  Victron MPPT
  test connector JST male
  ChargeMonitor 2018/11/03
  6V

custom parts:
  Generic connector 1 Pin: Generic male header
  Generic-4PinEdit: 4Pin edit pin labels
